# Fritzing sketch Fritzing final V2.0 (saved by Fritzing 0.9.3b)
breadboards: 1

parts:
  Composant1 = Arduino Uno (Rev3)
  L1 = Inductor [package="400 mil [THT]"]
  R3 = Resistor [tolerance=±5% resistance=1M package=THT]
  C1 = Ceramic Capacitor [capacitance=10nF package="100 mil [THT, multilayer]"]
  D1 = Rectifier Diode [part_number=1N4001 package="300 mil [THT]"]
  C2 = Ceramic Capacitor [capacitance=0.1nF package="100 mil [THT, multilayer]"]
  R4 = Resistor [tolerance=±5% resistance=220 package=THT]
  R5 = Resistor [tolerance=±5% resistance=10 package=THT]
  R6 = Resistor [tolerance=±5% resistance=220 package=THT]
  LED1 = LED - 5mm [color="Red (633nm)" package="5 mm [THT]"]
  LED2 = LED - 5mm [color="Blue (430nm)" package="5 mm [THT]"]
  LED3 = LED - 5mm [color="Green (560nm)" package="5 mm [THT]"]

nets:
  N1: Composant1.A0, Composant1.GND, R3.Pin_1, C1.0, C1.1, LED1.cathode, LED2.cathode, LED3.cathode
  N2: Composant1.D9_PWM, L1.pin_1
  N3: Composant1.D5_PWM, R5.Pin_0
  N4: Composant1.D6_PWM, R6.Pin_0
  N5: Composant1.D7, R4.Pin_0
  N6: L1.pin_0, D1.cathode, C2.1
  N7: R3.Pin_0, D1.anode
  N8: R4.Pin_1, LED1.anode
  N9: R5.Pin_1, LED2.anode
  N10: R6.Pin_1, LED3.anode
